// Logisim project ALU_Completo-CI.circ as structural Verilog: 4 circuits, main circuit main
module main (
  input  [3:0] X,
  input  [3:0] Y,
  input  [1:0] a0_a1,
  input  a2,
  input  Cin
);

  wire and_1_out, au_1_cout, au_1_s0, au_1_s1, au_1_s2, au_1_s3, lu_1_s0, lu_1_s1, lu_1_s2, lu_1_s3,
       n74157_1_pin4, n74157_1_pin7, n74157_1_pin9, n74157_1_pin12, n74157_1_pin15, not_1_out;

  AU au_1 (
    .X3(X[3]), .X2(X[2]), .X1(X[1]), .X0(X[0]), .Y0(Y[0]), .Y1(Y[1]), .Y2(Y[2]), .Y3(Y[3]), .a1(a0_a1[1]),
    .a0(a0_a1[0]), .Cin(Cin), .Cout(au_1_cout), .S3(au_1_s3), .S2(au_1_s2), .S1(au_1_s1), .S0(au_1_s0));
  LU lu_1 (
    .X0(X[0]), .Y0(Y[0]), .X1(X[1]), .Y1(Y[1]), .a0(a0_a1[0]), .a1(a0_a1[1]), .X2(X[2]), .Y2(Y[2]),
    .X3(X[3]), .Y3(Y[3]), .S0(lu_1_s0), .S1(lu_1_s1), .S2(lu_1_s2), .S3(lu_1_s3));
  and and_1 (and_1_out, au_1_cout, not_1_out);
  not not_1 (not_1_out, a2);
  _74157 #(.ShowInternalStructure("true")) u_74157_1 (
    .pin1(a2), .pin2(au_1_s0), .pin3(lu_1_s0), .pin4(n74157_1_pin4), .pin5(au_1_s1), .pin6(lu_1_s1),
    .pin7(n74157_1_pin7), .pin15(n74157_1_pin15), .pin14(au_1_s3), .pin13(lu_1_s3), .pin12(n74157_1_pin12),
    .pin11(au_1_s2), .pin10(lu_1_s2), .pin9(n74157_1_pin9));
  LED S0 (.in(n74157_1_pin4));
  LED S1 (.in(n74157_1_pin7));
  LED S2 (.in(n74157_1_pin9));
  LED S3 (.in(n74157_1_pin12));
  LED Cout (.in(and_1_out));
  // also tied to GND on the sheet: n74157_1_pin15
endmodule

module AU (
  input  X3,
  input  X2,
  input  X1,
  input  X0,
  input  Y0,
  input  Y1,
  input  Y2,
  input  Y3,
  input  a1,
  input  a0,
  input  Cin,
  output Cout,
  output S3,
  output S2,
  output S1,
  output S0
);

  wire and_2_out, n7404_1_pin2, n7404_1_pin4, n7404_1_pin6, n7404_1_pin8, n7404_1_pin10, n7404_1_pin12,
       n74153_1_pin1, n74153_1_pin3, n74153_1_pin5, n74153_1_pin7, n74153_1_pin9, n74153_1_pin11,
       n74153_1_pin13, n74153_1_pin15, n74153_2_pin1, n74153_2_pin3, n74153_2_pin5, n74153_2_pin7,
       n74153_2_pin9, n74153_2_pin11, n74153_2_pin13, n74153_2_pin15, n74283_1_pin7, n74283_1_pin9;

  _7404 #(.ShowInternalStructure("true")) u_7404_1 (
    .pin1(Y0), .pin2(n7404_1_pin2), .pin3(a1), .pin4(n7404_1_pin4), .pin5(a0), .pin6(n7404_1_pin6),
    .pin13(Y3), .pin12(n7404_1_pin12), .pin11(Y2), .pin10(n7404_1_pin10), .pin9(Y1), .pin8(n7404_1_pin8));
  _74153 #(.ShowInternalStructure("true")) u_74153_1 (
    .pin1(n74153_1_pin1), .pin2(a1), .pin3(n74153_1_pin3), .pin4(n7404_1_pin12), .pin5(n74153_1_pin5),
    .pin6(Y3), .pin7(n74153_1_pin7), .pin15(n74153_1_pin15), .pin14(a0), .pin13(n74153_1_pin13),
    .pin12(n7404_1_pin10), .pin11(n74153_1_pin11), .pin10(Y2), .pin9(n74153_1_pin9));
  _74153 #(.ShowInternalStructure("true")) u_74153_2 (
    .pin1(n74153_2_pin1), .pin2(a1), .pin3(n74153_2_pin3), .pin4(n7404_1_pin8), .pin5(n74153_2_pin5),
    .pin6(Y1), .pin7(n74153_2_pin7), .pin15(n74153_2_pin15), .pin14(a0), .pin13(n74153_2_pin13),
    .pin12(n7404_1_pin2), .pin11(n74153_2_pin11), .pin10(Y0), .pin9(n74153_2_pin9));
  _74283 #(.ShowInternalStructure("true")) u_74283_1 (
    .pin1(S1), .pin2(n74153_2_pin7), .pin3(X1), .pin4(S0), .pin5(X0), .pin6(n74153_2_pin9),
    .pin7(n74283_1_pin7), .pin15(n74153_1_pin9), .pin14(X2), .pin13(S2), .pin12(X3), .pin11(n74153_1_pin7),
    .pin10(S3), .pin9(n74283_1_pin9));
  and and_1 (Cout, n74283_1_pin9, n7404_1_pin4);
  or or_1 (n74283_1_pin7, a1, and_2_out);
  and and_2 (and_2_out, n7404_1_pin6, Cin, n7404_1_pin4);
  // also tied to GND on the sheet: {n74153_1_pin1, n74153_1_pin5, n74153_2_pin1, n74153_2_pin5, n74153_1_pin15, n74153_1_pin11, n74153_2_pin15, n74153_2_pin13}
  // also tied to VCC on the sheet: {n74153_1_pin3, n74153_2_pin3, n74153_1_pin13, n74153_2_pin11}
endmodule

module LU (
  input  X0,
  input  Y0,
  input  X1,
  input  Y1,
  input  a0,
  input  a1,
  input  X2,
  input  Y2,
  input  X3,
  input  Y3,
  output S0,
  output S1,
  output S2,
  output S3
);

  wire n7404_1_pin2, n7404_1_pin4, n7404_1_pin10, n7404_1_pin12, n7408_1_pin3, n7408_1_pin6, n7408_1_pin8,
       n7408_1_pin11, n7432_1_pin3, n7432_1_pin6, n7432_1_pin8, n7432_1_pin11, n7486_1_pin3, n7486_1_pin6,
       n7486_1_pin8, n7486_1_pin11, n74153_1_pin1, n74153_1_pin15, n74153_2_pin1, n74153_2_pin15;

  _7408 #(.ShowInternalStructure("true")) u_7408_1 (
    .pin1(X2), .pin2(Y2), .pin3(n7408_1_pin3), .pin4(X3), .pin5(Y3), .pin6(n7408_1_pin6), .pin13(X0),
    .pin12(Y0), .pin11(n7408_1_pin11), .pin10(X1), .pin9(Y1), .pin8(n7408_1_pin8));
  _7432 #(.ShowInternalStructure("true")) u_7432_1 (
    .pin1(X2), .pin2(Y2), .pin3(n7432_1_pin3), .pin4(X3), .pin5(Y3), .pin6(n7432_1_pin6), .pin13(X0),
    .pin12(Y0), .pin11(n7432_1_pin11), .pin10(X1), .pin9(Y1), .pin8(n7432_1_pin8));
  _7486 #(.ShowInternalStructure("true")) u_7486_1 (
    .pin1(X2), .pin2(Y2), .pin3(n7486_1_pin3), .pin4(X3), .pin5(Y3), .pin6(n7486_1_pin6), .pin13(X0),
    .pin12(Y0), .pin11(n7486_1_pin11), .pin10(X1), .pin9(Y1), .pin8(n7486_1_pin8));
  _7404 #(.ShowInternalStructure("true")) u_7404_1 (
    .pin1(X2), .pin2(n7404_1_pin2), .pin3(X3), .pin4(n7404_1_pin4), .pin13(X0), .pin12(n7404_1_pin12),
    .pin11(X1), .pin10(n7404_1_pin10));  // open: pin5, pin6, pin9, pin8
  _74153 #(.ShowInternalStructure("true")) u_74153_1 (
    .pin1(n74153_1_pin1), .pin2(a1), .pin3(n7404_1_pin12), .pin4(n7486_1_pin11), .pin5(n7432_1_pin11),
    .pin6(n7408_1_pin11), .pin7(S0), .pin15(n74153_1_pin15), .pin14(a0), .pin13(n7404_1_pin10),
    .pin12(n7486_1_pin8), .pin11(n7432_1_pin8), .pin10(n7408_1_pin8), .pin9(S1));
  _74153 #(.ShowInternalStructure("true")) u_74153_2 (
    .pin1(n74153_2_pin1), .pin2(a1), .pin3(n7404_1_pin2), .pin4(n7486_1_pin3), .pin5(n7432_1_pin3),
    .pin6(n7408_1_pin3), .pin7(S2), .pin15(n74153_2_pin15), .pin14(a0), .pin13(n7404_1_pin4),
    .pin12(n7486_1_pin6), .pin11(n7432_1_pin6), .pin10(n7408_1_pin6), .pin9(S3));
  // also tied to GND on the sheet: {n74153_1_pin1, n74153_2_pin1, n74153_1_pin15, n74153_2_pin15}
endmodule

module ALU_Completo (
  input  a2,
  input  a1,
  input  a0,
  input  Cin,
  input  X0,
  input  Y0,
  input  X1,
  input  Y1,
  input  X2,
  input  Y2,
  input  X3,
  input  Y3
);

  wire n7404_1_pin2, n7404_1_pin4, n7404_1_pin6, n7404_1_pin8, n7404_1_pin10, n7404_1_pin12, n7404_2_pin2,
       n7404_2_pin4, n7404_2_pin6, n7404_2_pin10, n7404_2_pin12, n7408_1_pin3, n7408_1_pin6, n7408_1_pin8,
       n7408_1_pin11, n7408_2_pin3, n7408_2_pin8, n7408_2_pin11, n7432_1_pin3, n7432_1_pin6, n7432_1_pin8,
       n7432_1_pin11, n7432_2_pin13, n7486_1_pin3, n7486_1_pin6, n7486_1_pin8, n7486_1_pin11, n74153_1_pin1,
       n74153_1_pin3, n74153_1_pin5, n74153_1_pin7, n74153_1_pin9, n74153_1_pin11, n74153_1_pin13,
       n74153_1_pin15, n74153_2_pin1, n74153_2_pin3, n74153_2_pin5, n74153_2_pin7, n74153_2_pin9,
       n74153_2_pin11, n74153_2_pin13, n74153_2_pin15, n74153_3_pin1, n74153_3_pin7, n74153_3_pin9,
       n74153_3_pin15, n74153_4_pin1, n74153_4_pin7, n74153_4_pin9, n74153_4_pin15, n74157_1_pin4,
       n74157_1_pin7, n74157_1_pin9, n74157_1_pin12, n74157_1_pin15, n74283_1_pin1, n74283_1_pin4,
       n74283_1_pin7, n74283_1_pin9, n74283_1_pin10, n74283_1_pin13;

  _7404 u_7404_1 (
    .pin1(Y0), .pin2(n7404_1_pin2), .pin3(a1), .pin4(n7404_1_pin4), .pin5(a0), .pin6(n7404_1_pin6),
    .pin13(Y3), .pin12(n7404_1_pin12), .pin11(Y2), .pin10(n7404_1_pin10), .pin9(Y1), .pin8(n7404_1_pin8));
  _74153 u_74153_1 (
    .pin1(n74153_1_pin1), .pin2(a1), .pin3(n74153_1_pin3), .pin4(n7404_1_pin12), .pin5(n74153_1_pin5),
    .pin6(Y3), .pin7(n74153_1_pin7), .pin15(n74153_1_pin15), .pin14(a0), .pin13(n74153_1_pin13),
    .pin12(n7404_1_pin10), .pin11(n74153_1_pin11), .pin10(Y2), .pin9(n74153_1_pin9));
  _74153 u_74153_2 (
    .pin1(n74153_2_pin1), .pin2(a1), .pin3(n74153_2_pin3), .pin4(n7404_1_pin8), .pin5(n74153_2_pin5),
    .pin6(Y1), .pin7(n74153_2_pin7), .pin15(n74153_2_pin15), .pin14(a0), .pin13(n74153_2_pin13),
    .pin12(n7404_1_pin2), .pin11(n74153_2_pin11), .pin10(Y0), .pin9(n74153_2_pin9));
  _7408 #(.ShowInternalStructure("true")) u_7408_1 (
    .pin1(X2), .pin2(Y2), .pin3(n7408_1_pin3), .pin4(X3), .pin5(Y3), .pin6(n7408_1_pin6), .pin13(X0),
    .pin12(Y0), .pin11(n7408_1_pin11), .pin10(X1), .pin9(Y1), .pin8(n7408_1_pin8));
  _7432 #(.ShowInternalStructure("true")) u_7432_1 (
    .pin1(X2), .pin2(Y2), .pin3(n7432_1_pin3), .pin4(X3), .pin5(Y3), .pin6(n7432_1_pin6), .pin13(X0),
    .pin12(Y0), .pin11(n7432_1_pin11), .pin10(X1), .pin9(Y1), .pin8(n7432_1_pin8));
  _7486 #(.ShowInternalStructure("true")) u_7486_1 (
    .pin1(X2), .pin2(Y2), .pin3(n7486_1_pin3), .pin4(X3), .pin5(Y3), .pin6(n7486_1_pin6), .pin13(X0),
    .pin12(Y0), .pin11(n7486_1_pin11), .pin10(X1), .pin9(Y1), .pin8(n7486_1_pin8));
  _7404 #(.ShowInternalStructure("true")) u_7404_2 (
    .pin1(X2), .pin2(n7404_2_pin2), .pin3(X3), .pin4(n7404_2_pin4), .pin5(a2), .pin6(n7404_2_pin6),
    .pin13(X0), .pin12(n7404_2_pin12), .pin11(X1), .pin10(n7404_2_pin10));  // open: pin9, pin8
  _74283 u_74283_1 (
    .pin1(n74283_1_pin1), .pin2(n74153_2_pin7), .pin3(X1), .pin4(n74283_1_pin4), .pin5(X0),
    .pin6(n74153_2_pin9), .pin7(n74283_1_pin7), .pin15(n74153_1_pin9), .pin14(X2), .pin13(n74283_1_pin13),
    .pin12(X3), .pin11(n74153_1_pin7), .pin10(n74283_1_pin10), .pin9(n74283_1_pin9));
  _74153 #(.ShowInternalStructure("true")) u_74153_3 (
    .pin1(n74153_3_pin1), .pin2(a1), .pin3(n7404_2_pin12), .pin4(n7486_1_pin11), .pin5(n7432_1_pin11),
    .pin6(n7408_1_pin11), .pin7(n74153_3_pin7), .pin15(n74153_3_pin15), .pin14(a0), .pin13(n7404_2_pin10),
    .pin12(n7486_1_pin8), .pin11(n7432_1_pin8), .pin10(n7408_1_pin8), .pin9(n74153_3_pin9));
  _74153 u_74153_4 (
    .pin1(n74153_4_pin1), .pin2(a1), .pin3(n7404_2_pin2), .pin4(n7486_1_pin3), .pin5(n7432_1_pin3),
    .pin6(n7408_1_pin3), .pin7(n74153_4_pin7), .pin15(n74153_4_pin15), .pin14(a0), .pin13(n7404_2_pin4),
    .pin12(n7486_1_pin6), .pin11(n7432_1_pin6), .pin10(n7408_1_pin6), .pin9(n74153_4_pin9));
  _7432 #(.ShowInternalStructure("true")) u_7432_2 (
    .pin13(n7432_2_pin13), .pin12(a1), .pin11(n74283_1_pin7));  // open: pin1, pin2, pin3, pin4, pin5, pin6, pin10, pin9, pin8
  _7408 #(.ShowInternalStructure("true")) u_7408_2 (
    .pin1(Cin), .pin2(n7404_1_pin6), .pin3(n7408_2_pin3), .pin4(n7408_2_pin3), .pin5(n7404_1_pin4),
    .pin6(n7432_2_pin13), .pin13(n74283_1_pin9), .pin12(n7404_1_pin4), .pin11(n7408_2_pin11),
    .pin10(n7408_2_pin11), .pin9(n7404_2_pin6), .pin8(n7408_2_pin8));
  _74157 #(.ShowInternalStructure("true")) u_74157_1 (
    .pin1(a2), .pin2(n74283_1_pin4), .pin3(n74153_3_pin7), .pin4(n74157_1_pin4), .pin5(n74283_1_pin1),
    .pin6(n74153_3_pin9), .pin7(n74157_1_pin7), .pin15(n74157_1_pin15), .pin14(n74283_1_pin10),
    .pin13(n74153_4_pin9), .pin12(n74157_1_pin12), .pin11(n74283_1_pin13), .pin10(n74153_4_pin7),
    .pin9(n74157_1_pin9));
  LED Cout (.in(n7408_2_pin8));
  LED S3 (.in(n74157_1_pin12));
  LED S2 (.in(n74157_1_pin9));
  LED S1 (.in(n74157_1_pin7));
  LED S0 (.in(n74157_1_pin4));
  // also tied to GND on the sheet: {n74153_1_pin1, n74153_1_pin5, n74153_2_pin1, n74153_2_pin5, n74153_1_pin15, n74153_1_pin11, n74153_2_pin15, n74153_2_pin13, n74153_3_pin1, n74153_4_pin1, n74153_3_pin15, n74153_4_pin15, n74157_1_pin15}
  // also tied to VCC on the sheet: {n74153_1_pin3, n74153_2_pin3, n74153_1_pin13, n74153_2_pin11}
endmodule
